// Logisim project lab1_3.circ as structural Verilog: 2 circuits, main circuit main
module _4_1MUX (
  input  D0,
  input  D1,
  input  D2,
  input  D3,
  input  S0,
  input  S1,
  output out_7
);

  wire main_1_out_4, main_2_out_4;

  main main_1 (.D0(D0), .D1(D1), .S(S0), .out_4(main_1_out_4));
  main main_2 (.D0(D2), .D1(D3), .S(S0), .out_4(main_2_out_4));
  main main_3 (.D0(main_1_out_4), .D1(main_2_out_4), .S(S1), .out_4(out_7));

  // Notes on the sheet:
  //   4-1MUX
  //   2-1MUX
  //   2-1MUX
  //   2-1MUX
endmodule

module main (
  input  D0,
  input  D1,
  input  S,
  output out_4
);

  wire transistor_1_out;

  Transistor transistor_1 (.in(1'b1), .out(transistor_1_out), .gate(S));
  Transistor #(.\type ("n")) transistor_2 (.in(1'b0), .out(transistor_1_out), .gate(S));
  // Transmission_Gate transmission_1: pin names not known; wires that end beside it: D0, S, transistor_1_out, out_4
  // Transmission_Gate transmission_2: pin names not known; wires that end beside it: D1, transistor_1_out, S, out_4
endmodule
