// Logisim project lab2_2.circ as structural Verilog: 1 circuit, main circuit main
module main (
  input  i0,
  input  i1,
  input  i2,
  input  i3,
  input  i4,
  input  i5,
  input  i6,
  input  i7
);

  wire _0_out, _1_out, _2_out, _3_out, _4_out, _5_out, _6_out, not_1_out, not_2_out, not_3_out, not_4_out,
       not_5_out, not_6_out, not_7_out, not_8_out, not_9_out, not_10_out, not_11_out, not_12_out, not_13_out,
       not_14_out, not_15_out, not_16_out, not_17_out, not_18_out, not_19_out, not_21_out, not_22_out,
       not_23_out, not_24_out, not_25_out, not_26_out, not_27_out, not_28_out, undriven;
  wire [2:0] o2_out;

  not not_1 (not_1_out, i0);
  not not_2 (not_2_out, i0);
  not not_3 (not_3_out, i1);
  not not_4 (not_4_out, i0);
  not not_5 (not_5_out, i1);
  not not_6 (not_6_out, i2);
  not not_7 (not_7_out, i0);
  not not_8 (not_8_out, i1);
  not not_9 (not_9_out, i2);
  not not_10 (not_10_out, i3);
  not not_11 (not_11_out, i0);
  not not_12 (not_12_out, i1);
  not not_13 (not_13_out, i2);
  not not_14 (not_14_out, i3);
  not not_15 (not_15_out, i4);
  not not_16 (not_16_out, i0);
  not not_17 (not_17_out, i1);
  not not_18 (not_18_out, i2);
  not not_19 (not_19_out, i3);
  not not_20 (not_19_out, i4);
  not not_21 (not_21_out, i5);
  not not_22 (not_22_out, i0);
  not not_23 (not_23_out, i1);
  not not_24 (not_24_out, i2);
  not not_25 (not_25_out, i3);
  not not_26 (not_26_out, i4);
  not not_27 (not_27_out, i5);
  not not_28 (not_28_out, i6);
  and _0 (_0_out, not_1_out, i1);
  and _1 (_1_out, not_2_out, not_3_out, i2);
  and _2 (_2_out, not_4_out, not_5_out, not_6_out, i3);
  and _3 (_3_out, not_7_out, not_8_out, not_9_out, not_10_out, i4);
  and _4 (_4_out, not_11_out, not_12_out, not_13_out, not_14_out, not_15_out, i5);
  and _5 (_5_out, not_16_out, not_17_out, not_18_out, not_19_out, not_19_out, not_21_out, i6);
  and _6 (_6_out, not_22_out, not_23_out, not_24_out, not_25_out, not_26_out, not_27_out, not_28_out, i7);
  or o0 (o2_out[2], _4_out, _5_out, _3_out, _6_out);
  or o1 (o2_out[1], _5_out, _1_out, _2_out, _6_out);
  or o2 (o2_out[0], _0_out, _2_out, _4_out, _6_out);
  Hex_Digit_Display hex_digit_display_1 (.value({1'b0, o2_out}), .dp(undriven));
  Hex_Digit_Display hex_digit_display_2 (.value({1'b0, o2_out}), .dp(undriven));

  // Notes on the sheet:
  //   8-3优先权编码器
endmodule
