// Logisim project lab2_3.circ as structural Verilog: 2 circuits, main circuit main
module main (
  input  A,
  input  B,
  input  CIN,
  output COUT,
  output out_5
);

  wire and_1_out, and_2_out, and_3_out, xor_1_out;

  and and_1 (and_1_out, A, CIN);
  and and_2 (and_2_out, A, B);
  and and_3 (and_3_out, B, CIN);
  or or_1 (COUT, and_1_out, and_2_out, and_3_out);
  xor xor_1 (xor_1_out, A, B);
  xor xor_2 (out_5, xor_1_out, CIN);

  // Notes on the sheet:
  //   FA全加器
endmodule

module _4FA (
  input  in_1,
  input  in_2,
  input  in_3,
  input  in_4,
  input  in_5,
  input  in_6,
  input  in_7,
  input  in_8,
  input  in_9,
  output out_10,
  output out_11,
  output out_12,
  output out_13,
  output out_14
);

  wire main_2_cout, main_3_cout, main_4_cout;

  Hex_Digit_Display hex_digit_display_1 (.value({in_8, in_6, in_4, in_3}));  // open: dp
  Hex_Digit_Display hex_digit_display_2 (.value({in_9, in_7, in_5, in_2}));  // open: dp
  main main_1 ();  // open: A, B, CIN, COUT, out_5
  main main_2 (.A(in_1), .B(in_3), .CIN(in_2), .COUT(main_2_cout), .out_5(out_10));
  main main_3 (.A(main_2_cout), .B(in_4), .CIN(in_5), .COUT(main_3_cout), .out_5(out_11));
  main main_4 (.A(main_3_cout), .B(in_6), .CIN(in_7), .COUT(main_4_cout), .out_5(out_12));
  main main_5 (.A(main_4_cout), .B(in_8), .CIN(in_9), .COUT(out_14), .out_5(out_13));
  Hex_Digit_Display hex_digit_display_3 (.value({out_13, out_12, out_11, out_10}));  // open: dp
endmodule
