// Logisim project lab2_4.circ as structural Verilog: 3 circuits, main circuit main
module main (
  input  D0,
  input  D1,
  input  S,
  output Y
);

  wire transistor_1_out;

  Transistor transistor_1 (.in(1'b1), .out(transistor_1_out), .gate(S));
  Transistor #(.\type ("n")) transistor_2 (.in(1'b0), .out(transistor_1_out), .gate(S));
  // Transmission_Gate transmission_1: pin names not known; wires that end beside it: D0, S, transistor_1_out, Y
  // Transmission_Gate transmission_2: pin names not known; wires that end beside it: D1, transistor_1_out, S, Y

  // Notes on the sheet:
  //   2选1多路选择器
endmodule

module _8_1MUX (
  input  S3,
  input  S2,
  input  S1,
  input  A1,
  input  A2,
  input  A3,
  input  A4,
  input  A5,
  input  A6,
  input  A7,
  input  A8,
  output out_12
);

  wire and_1_out, and_2_out, main_1_y, main_2_y, main_3_y, main_4_y, main_5_y, main_6_y, not_1_out;

  main main_1 (.D0(A1), .D1(A2), .S(S3), .Y(main_1_y));
  main main_2 (.D0(A3), .D1(A4), .S(S3), .Y(main_2_y));
  main main_3 (.D0(A5), .D1(A6), .S(S3), .Y(main_3_y));
  main main_4 (.D0(A7), .D1(A8), .S(S3), .Y(main_4_y));
  not not_1 (not_1_out, S1);
  main main_5 (.D0(main_1_y), .D1(main_2_y), .S(S2), .Y(main_5_y));
  main main_6 (.D0(main_3_y), .D1(main_4_y), .S(S2), .Y(main_6_y));
  and and_1 (and_1_out, not_1_out, main_5_y);
  and and_2 (and_2_out, S1, main_6_y);
  or or_1 (out_12, and_1_out, and_2_out);
endmodule

module ALU (
  input  in_1,
  input  in_2,
  input  in_3,
  input  in_4,
  input  in_5,
  input  in_6,
  output out_7
);

  wire adder_1_out, and_1_out, not_1_out, not_2_out, or_1_out, subtractor_1_out, xor_1_out;

  Adder #(.width(1)) adder_1 (.a(in_2), .b(in_3), .out(adder_1_out), .cin(in_1));  // open: cout
  Subtractor #(.width(1)) subtractor_1 (.a(in_2), .b(in_3), .out(subtractor_1_out));  // open: bin, bout
  and and_1 (and_1_out, in_2, in_3);
  or or_1 (or_1_out, in_2, in_3);
  xor xor_1 (xor_1_out, in_2, in_3);
  not not_1 (not_1_out, in_2);
  not not_2 (not_2_out, in_3);
  _8_1MUX u_8_1mux_1 (
    .S3(in_6), .S2(in_5), .S1(in_4), .A1(adder_1_out), .A2(subtractor_1_out), .A3(and_1_out), .A4(or_1_out),
    .A5(xor_1_out), .A6(not_1_out), .A7(in_2), .A8(not_2_out), .out_12(out_7));
endmodule
