// Logisim project lab2_FA.circ as structural Verilog: 1 circuit, main circuit main
module main (
  input  A,
  input  B,
  input  CIN,
  output COUT,
  output out_5
);

  wire and_1_out, and_2_out, and_3_out, xor_1_out;

  and and_1 (and_1_out, A, CIN);
  and and_2 (and_2_out, A, B);
  and and_3 (and_3_out, B, CIN);
  or or_1 (COUT, and_1_out, and_2_out, and_3_out);
  xor xor_1 (xor_1_out, A, B);
  xor xor_2 (out_5, xor_1_out, CIN);

  // Notes on the sheet:
  //   FA全加器
endmodule
