// Logisim project LAB3-1.circ as structural Verilog: 3 circuits, main circuit main
module main (
  input  CLK,
  input  LD,
  input  CLR,
  input  DO,
  input  D1,
  input  D2,
  input  D3,
  input  ENP,
  input  ENT,
  output Q0,
  output Q1,
  output Q2,
  output Q3,
  output RCO
);

  wire and_1_out, and_2_out, and_3_out, and_4_out, and_5_out, and_6_out, and_7_out, and_8_out, and_10_out,
       and_11_out, and_12_out, and_13_out, and_14_out, and_15_out, and_16_out, and_17_out, buffer_1_out,
       d_ff_1_qn, d_ff_2_qn, d_ff_3_qn, d_ff_4_qn, not_1_out, not_2_out, not_3_out, or_1_out, or_2_out,
       or_3_out, or_4_out, xor_1_out, xor_2_out, xor_3_out, xor_4_out;

  and and_1 (and_1_out, ENP, ENT);
  not not_1 (not_1_out, CLK);
  buf buffer_1 (buffer_1_out, CLR);
  not not_2 (not_2_out, d_ff_1_qn);
  and and_2 (and_2_out, not_2_out, and_1_out);
  and and_3 (and_3_out, ~d_ff_2_qn, ~d_ff_1_qn);  // AND_Gate
  and and_4 (and_4_out, and_3_out, and_1_out);
  and and_5 (and_5_out, ~d_ff_3_qn, ~d_ff_2_qn, ~d_ff_1_qn);  // AND_Gate
  not not_3 (not_3_out, ENT);
  and and_6 (and_6_out, LD, ~buffer_1_out);  // AND_Gate
  and and_7 (and_7_out, ~and_6_out, ~buffer_1_out);  // AND_Gate
  xor xor_1 (xor_1_out, and_1_out, ~d_ff_1_qn);  // XOR_Gate
  xor xor_2 (xor_2_out, and_2_out, ~d_ff_2_qn);  // XOR_Gate
  xor xor_3 (xor_3_out, and_4_out, ~d_ff_3_qn);  // XOR_Gate
  and and_8 (and_8_out, and_5_out, and_1_out);
  xor xor_4 (xor_4_out, and_8_out, ~d_ff_4_qn);  // XOR_Gate
  and and_9 (RCO, ~d_ff_4_qn, ~d_ff_3_qn, ~d_ff_2_qn, ~d_ff_1_qn, ~not_3_out);  // AND_Gate
  and and_10 (and_10_out, and_6_out, DO);
  and and_11 (and_11_out, and_7_out, xor_1_out);
  and and_12 (and_12_out, and_6_out, D1);
  and and_13 (and_13_out, and_7_out, xor_2_out);
  and and_14 (and_14_out, and_6_out, D2);
  and and_15 (and_15_out, and_7_out, xor_3_out);
  and and_16 (and_16_out, and_6_out, D3);
  and and_17 (and_17_out, and_7_out, xor_4_out);
  or or_1 (or_1_out, and_10_out, and_11_out);
  or or_2 (or_2_out, and_12_out, and_13_out);
  or or_3 (or_3_out, and_14_out, and_15_out);
  or or_4 (or_4_out, and_16_out, and_17_out);
  D_Flip_Flop d_ff_1 (.clk(not_1_out), .D(or_1_out), .Q(Q0), .Qn(d_ff_1_qn));  // open: preset, reset
  D_Flip_Flop d_ff_2 (.clk(not_1_out), .D(or_2_out), .Q(Q1), .Qn(d_ff_2_qn));  // open: preset, reset
  D_Flip_Flop d_ff_3 (.clk(not_1_out), .D(or_3_out), .Q(Q2), .Qn(d_ff_3_qn));  // open: preset, reset
  D_Flip_Flop d_ff_4 (.clk(not_1_out), .D(or_4_out), .Q(Q3), .Qn(d_ff_4_qn));  // open: preset, reset
endmodule

module \置位计数6_15  (
  input  in_1,
  input  in_2,
  input  in_3
);

  wire and_1_out, clock_1_out, main_1_rco, not_1_out, not_2_out;
  wire [3:0] main_1_q0;

  Clock clock_1 (.out(clock_1_out));
  not not_1 (not_1_out, and_1_out);
  not not_2 (not_2_out, and_1_out);
  main main_1 (
    .CLK(clock_1_out), .LD(and_1_out), .CLR(in_1), .DO(not_1_out), .D1(and_1_out), .D2(and_1_out),
    .D3(not_2_out), .ENP(in_2), .ENT(in_3), .Q0(main_1_q0[0]), .Q1(main_1_q0[1]), .Q2(main_1_q0[2]),
    .Q3(main_1_q0[3]), .RCO(main_1_rco));
  Hex_Digit_Display hex_digit_display_1 (.value(main_1_q0));  // open: dp
  LED led_1 (.in(main_1_rco));
  and and_1 (and_1_out, main_1_q0[0], main_1_q0[1], main_1_q0[2], main_1_q0[3]);
endmodule

module \清零计数0_9  (
  input  in_1,
  input  in_2,
  input  in_3,
  input  in_4,
  input  in_5,
  input  in_6,
  input  in_7
);

  wire and_1_out, clock_1_out, main_1_rco;
  wire [3:0] main_1_q0;

  Clock clock_1 (.out(clock_1_out));
  main main_1 (
    .CLK(clock_1_out), .LD(in_1), .CLR(and_1_out), .DO(in_2), .D1(in_3), .D2(in_4), .D3(in_5), .ENP(in_6),
    .ENT(in_7), .Q0(main_1_q0[0]), .Q1(main_1_q0[1]), .Q2(main_1_q0[2]), .Q3(main_1_q0[3]), .RCO(main_1_rco));
  Hex_Digit_Display hex_digit_display_1 (.value(main_1_q0), .dp(1'b0));
  LED led_1 (.in(main_1_rco));
  and and_1 (and_1_out, main_1_q0[3], main_1_q0[0]);
endmodule
