// Logisim project LAB3-3.circ as structural Verilog: 1 circuit, main circuit main
module main (
  input  [4:0] RA,
  input  [4:0] RB,
  input  [4:0] RW,
  input  [31:0] BUSW,
  input  WE,
  output [31:0] busA,
  output [31:0] busB
);

  wire and_1_out, and_2_out, and_3_out, and_4_out, and_5_out, and_6_out, and_7_out, and_8_out, and_9_out,
       and_10_out, and_11_out, and_12_out, and_13_out, and_14_out, and_15_out, and_16_out, and_17_out,
       and_18_out, and_19_out, and_20_out, and_21_out, and_22_out, and_23_out, and_24_out, and_25_out,
       and_26_out, and_27_out, and_28_out, and_29_out, and_30_out, and_31_out, and_32_out, CLK_out,
       decoder_1_out0, decoder_1_out1, decoder_1_out2, decoder_1_out3, decoder_1_out4, decoder_1_out5,
       decoder_1_out6, decoder_1_out7, decoder_1_out8, decoder_1_out9, decoder_1_out10, decoder_1_out11,
       decoder_1_out12, decoder_1_out13, decoder_1_out14, decoder_1_out15, decoder_1_out16, decoder_1_out17,
       decoder_1_out18, decoder_1_out19, decoder_1_out20, decoder_1_out21, decoder_1_out22, decoder_1_out23,
       decoder_1_out24, decoder_1_out25, decoder_1_out26, decoder_1_out27, decoder_1_out28, decoder_1_out29,
       decoder_1_out30, decoder_1_out31, undriven, undriven_2, undriven_3, undriven_4, undriven_5;
  wire [31:0] _0_q, _1_q, _2_q, _3_q, _4_q, _5_q, _6_q, _7_q, _8_q, _9_q, _10_q, _11_q, _12_q, _13_q, _14_q,
       _15_q, _16_q, _17_q, _18_q, _19_q, _20_q, _21_q, _22_q, _23_q, _24_q, _25_q, _26_q, _27_q, _28_q,
       _29_q, _30_q, _31_q;

  Decoder #(.select(5), .enable("false")) decoder_1 (
    .out0(decoder_1_out0), .out1(decoder_1_out1), .out2(decoder_1_out2), .out3(decoder_1_out3),
    .out4(decoder_1_out4), .out5(decoder_1_out5), .out6(decoder_1_out6), .out7(decoder_1_out7),
    .out8(decoder_1_out8), .out9(decoder_1_out9), .out10(decoder_1_out10), .out11(decoder_1_out11),
    .out12(decoder_1_out12), .out13(decoder_1_out13), .out14(decoder_1_out14), .out15(decoder_1_out15),
    .out16(decoder_1_out16), .out17(decoder_1_out17), .out18(decoder_1_out18), .out19(decoder_1_out19),
    .out20(decoder_1_out20), .out21(decoder_1_out21), .out22(decoder_1_out22), .out23(decoder_1_out23),
    .out24(decoder_1_out24), .out25(decoder_1_out25), .out26(decoder_1_out26), .out27(decoder_1_out27),
    .out28(decoder_1_out28), .out29(decoder_1_out29), .out30(decoder_1_out30), .out31(decoder_1_out31),
    .sel(RW));
  and and_1 (and_1_out, WE, CLK_out, decoder_1_out0);
  and and_2 (and_2_out, WE, CLK_out, decoder_1_out1);
  and and_3 (and_3_out, WE, CLK_out, decoder_1_out2);
  and and_4 (and_4_out, WE, CLK_out, decoder_1_out3);
  and and_5 (and_5_out, WE, CLK_out, decoder_1_out4);
  and and_6 (and_6_out, WE, CLK_out, decoder_1_out5);
  and and_7 (and_7_out, WE, CLK_out, decoder_1_out6);
  and and_8 (and_8_out, WE, CLK_out, decoder_1_out7);
  and and_9 (and_9_out, WE, CLK_out, decoder_1_out8);
  and and_10 (and_10_out, WE, CLK_out, decoder_1_out9);
  and and_11 (and_11_out, WE, CLK_out, decoder_1_out10);
  and and_12 (and_12_out, WE, CLK_out, decoder_1_out11);
  and and_13 (and_13_out, WE, CLK_out, decoder_1_out12);
  and and_14 (and_14_out, WE, CLK_out, decoder_1_out13);
  and and_15 (and_15_out, WE, CLK_out, decoder_1_out14);
  and and_16 (and_16_out, WE, CLK_out, decoder_1_out15);
  and and_17 (and_17_out, WE, CLK_out, decoder_1_out16);
  and and_18 (and_18_out, WE, CLK_out, decoder_1_out17);
  and and_19 (and_19_out, WE, CLK_out, decoder_1_out18);
  and and_20 (and_20_out, WE, CLK_out, decoder_1_out19);
  and and_21 (and_21_out, WE, CLK_out, decoder_1_out20);
  and and_22 (and_22_out, WE, CLK_out, decoder_1_out21);
  and and_23 (and_23_out, WE, CLK_out, decoder_1_out22);
  and and_24 (and_24_out, WE, CLK_out, decoder_1_out23);
  and and_25 (and_25_out, WE, CLK_out, decoder_1_out24);
  and and_26 (and_26_out, WE, CLK_out, decoder_1_out25);
  and and_27 (and_27_out, WE, CLK_out, decoder_1_out26);
  and and_28 (and_28_out, WE, CLK_out, decoder_1_out27);
  and and_29 (and_29_out, WE, CLK_out, decoder_1_out28);
  and and_30 (and_30_out, WE, CLK_out, decoder_1_out29);
  and and_31 (and_31_out, WE, CLK_out, decoder_1_out30);
  and and_32 (and_32_out, WE, CLK_out, decoder_1_out31);
  Clock CLK (.out(CLK_out));
  Register #(.width(32), .Select("low")) _0 (.D(BUSW), .Q(_0_q), .clk(and_1_out), .clr(undriven));  // open: en
  Register #(.width(32), .Select("low")) _1 (.D(BUSW), .Q(_1_q), .clk(and_2_out));  // open: en, clr
  Register #(.width(32), .Select("low")) _2 (.D(BUSW), .Q(_2_q), .clk(and_3_out));  // open: en, clr
  Register #(.width(32), .Select("low")) _3 (.D(BUSW), .Q(_3_q), .clk(and_4_out));  // open: en, clr
  Register #(.width(32), .Select("low")) _4 (.D(BUSW), .Q(_4_q), .clk(and_5_out));  // open: en, clr
  Register #(.width(32), .Select("low")) _5 (.D(BUSW), .Q(_5_q), .clk(and_6_out));  // open: en, clr
  Register #(.width(32), .Select("low")) _6 (.D(BUSW), .Q(_6_q), .clk(and_7_out));  // open: en, clr
  Register #(.width(32), .Select("low")) _7 (.D(BUSW), .Q(_7_q), .clk(and_8_out));  // open: en, clr
  Register #(.width(32), .Select("low")) _8 (.D(BUSW), .Q(_8_q), .clk(and_9_out), .clr(undriven_2));  // open: en
  Register #(.width(32), .Select("low")) _9 (.D(BUSW), .Q(_9_q), .clk(and_10_out));  // open: en, clr
  Register #(.width(32), .Select("low")) _10 (.D(BUSW), .Q(_10_q), .clk(and_11_out));  // open: en, clr
  Register #(.width(32), .Select("low")) _11 (.D(BUSW), .Q(_11_q), .clk(and_12_out));  // open: en, clr
  Register #(.width(32), .Select("low")) _12 (.D(BUSW), .Q(_12_q), .clk(and_13_out), .clr(undriven_3));  // open: en
  Register #(.width(32), .Select("low")) _13 (.D(BUSW), .Q(_13_q), .clk(and_14_out));  // open: en, clr
  Register #(.width(32), .Select("low")) _14 (.D(BUSW), .Q(_14_q), .clk(and_15_out));  // open: en, clr
  Register #(.width(32), .Select("low")) _15 (.D(BUSW), .Q(_15_q), .clk(and_16_out));  // open: en, clr
  Register #(.width(32), .Select("low")) _16 (.D(BUSW), .Q(_16_q), .clk(and_17_out));  // open: en, clr
  Register #(.width(32), .Select("low")) _17 (.D(BUSW), .Q(_17_q), .clk(and_18_out));  // open: en, clr
  Register #(.width(32), .Select("low")) _18 (.D(BUSW), .Q(_18_q), .clk(and_19_out));  // open: en, clr
  Register #(.width(32), .Select("low")) _19 (.D(BUSW), .Q(_19_q), .clk(and_20_out));  // open: en, clr
  Register #(.width(32), .Select("low")) _20 (.D(BUSW), .Q(_20_q), .clk(and_21_out), .clr(undriven_4));  // open: en
  Register #(.width(32), .Select("low")) _21 (.D(BUSW), .Q(_21_q), .clk(and_22_out));  // open: en, clr
  Register #(.width(32), .Select("low")) _22 (.D(BUSW), .Q(_22_q), .clk(and_23_out));  // open: en, clr
  Register #(.width(32), .Select("low")) _23 (.D(BUSW), .Q(_23_q), .clk(and_24_out));  // open: en, clr
  Register #(.width(32), .Select("low")) _24 (.D(BUSW), .Q(_24_q), .clk(and_25_out));  // open: en, clr
  Register #(.width(32), .Select("low")) _25 (.D(BUSW), .Q(_25_q), .clk(and_26_out));  // open: en, clr
  Register #(.width(32), .Select("low")) _26 (.D(BUSW), .Q(_26_q), .clk(and_27_out));  // open: en, clr
  Register #(.width(32), .Select("low")) _27 (.D(BUSW), .Q(_27_q), .clk(and_28_out));  // open: en, clr
  Register #(.width(32), .Select("low")) _28 (.D(BUSW), .Q(_28_q), .clk(and_29_out), .clr(undriven_5));  // open: en
  Register #(.width(32), .Select("low")) _29 (.D(BUSW), .Q(_29_q), .clk(and_30_out));  // open: en, clr
  Register #(.width(32), .Select("low")) _30 (.D(BUSW), .Q(_30_q), .clk(and_31_out));  // open: en, clr
  Register #(.width(32), .Select("low")) _31 (.D(BUSW), .Q(_31_q), .clk(and_32_out));  // open: en, clr
  Multiplexer #(.select(5), .width(32), .enable("false")) multiplexer_1 (
    .in0(_0_q), .in1(_1_q), .in2(_2_q), .in3(_3_q), .in4(_4_q), .in5(_5_q), .in6(_6_q), .in7(_7_q),
    .in8(_8_q), .in9(_9_q), .in10(_10_q), .in11(_11_q), .in12(_12_q), .in13(_13_q), .in14(_14_q),
    .in15(_15_q), .in16(_16_q), .in17(_17_q), .in18(_18_q), .in19(_19_q), .in20(_20_q), .in21(_21_q),
    .in22(_22_q), .in23(_23_q), .in24(_24_q), .in25(_25_q), .in26(_26_q), .in27(_27_q), .in28(_28_q),
    .in29(_29_q), .in30(_30_q), .in31(_31_q), .out(busB), .sel(RB));
  Multiplexer #(.select(5), .width(32), .enable("false")) multiplexer_2 (
    .in0(_0_q), .in1(_1_q), .in2(_2_q), .in3(_3_q), .in4(_4_q), .in5(_5_q), .in6(_6_q), .in7(_7_q),
    .in8(_8_q), .in9(_9_q), .in10(_10_q), .in11(_11_q), .in12(_12_q), .in13(_13_q), .in14(_14_q),
    .in15(_15_q), .in16(_16_q), .in17(_17_q), .in18(_18_q), .in19(_19_q), .in20(_20_q), .in21(_21_q),
    .in22(_22_q), .in23(_23_q), .in24(_24_q), .in25(_25_q), .in26(_26_q), .in27(_27_q), .in28(_28_q),
    .in29(_29_q), .in30(_30_q), .in31(_31_q), .out(busA), .sel(RA));
endmodule
