// Logisim project LAB 5-1.circ as structural Verilog: 1 circuit, main circuit main
module main (
  input  [11:0] \地址数据 ,
  input  [31:0] \输入数据 ,
  input  \输入使能 ,
  input  \片选 ,
  input  \输出使能 ,
  output [31:0] out_6
);

  wire \复位按钮_out , \时钟信号_out ;

  Clock \u_时钟信号  (.out(\时钟信号_out ));
  Button \u_复位按钮  (.out(\复位按钮_out ));
  RAM #(.addrWidth(12), .dataWidth(32), .bus("separate"), .Select("low")) \u_存储器RAM  (
    .addr(\地址数据 ), .din(\输入数据 ), .data(out_6), .str(\输入使能 ), .sel(\片选 ), .clk(\时钟信号_out ), .ld(\输出使能 ),
    .clr(\复位按钮_out ));
endmodule
