// Logisim project LAB 5-2.circ as structural Verilog: 15 circuits, main circuit CLU
module CLU (
  input  C0,
  input  G4,
  input  P4,
  input  G3,
  input  P3,
  input  G2,
  input  P2,
  input  G1,
  input  P1,
  output C4,
  output C3,
  output C2,
  output C1
);

  wire and_1_out, and_2_out, and_3_out, and_4_out, and_5_out, and_6_out, and_7_out, and_8_out, and_9_out,
       and_10_out;

  and and_1 (and_1_out, P4, G3);
  and and_2 (and_2_out, P4, P3, G2);
  or or_1 (C4, G4, and_1_out, and_2_out, and_3_out, and_4_out);
  and and_3 (and_3_out, P4, P3, P2, G1);
  and and_4 (and_4_out, P4, P3, P2, P1, C0);
  or or_2 (C3, G3, and_5_out, and_7_out, and_6_out);
  and and_5 (and_5_out, P3, G2);
  and and_6 (and_6_out, P3, P2, P1, C0);
  and and_7 (and_7_out, P3, P2, G1);
  or or_3 (C2, G2, and_8_out, and_9_out);
  and and_8 (and_8_out, P2, G1);
  and and_9 (and_9_out, P2, P1, C0);
  or or_4 (C1, G1, and_10_out);
  and and_10 (and_10_out, P1, C0);
endmodule

module \全加器  (
  input  A,
  input  B,
  input  C,
  output G,
  output P,
  output F
);

  wire xor_1_out;

  and and_1 (G, A, B);
  or or_1 (P, A, B);
  xor xor_1 (xor_1_out, A, B);
  xor xor_2 (F, xor_1_out, C);
endmodule

module \_4位加法器  (
  input  [3:0] B,
  input  [3:0] A,
  input  C0,
  output Gg,
  output Pg,
  output C4,
  output [3:0] S,
  output F3,
  output C3
);

  wire clu_1_c1, clu_1_c2, FA0_g, FA0_p, FA1_g, FA1_p, FA2_g, FA2_p, FA3_g, FA3_p;

  \全加器  FA3 (.A(A[3]), .B(B[3]), .C(C3), .G(FA3_g), .P(FA3_p), .F(F3));
  \全加器  FA2 (.A(A[2]), .B(B[2]), .C(clu_1_c2), .G(FA2_g), .P(FA2_p), .F(S[2]));
  \全加器  FA1 (.A(A[1]), .B(B[1]), .C(clu_1_c1), .G(FA1_g), .P(FA1_p), .F(S[1]));
  \全加器  FA0 (.A(A[0]), .B(B[0]), .C(C0), .G(FA0_g), .P(FA0_p), .F(S[0]));
  CLU clu_1 (
    .C0(C0), .C4(C4), .C3(C3), .C2(clu_1_c2), .C1(clu_1_c1), .G4(FA3_g), .P4(FA3_p), .G3(FA2_g), .P3(FA2_p),
    .G2(FA1_g), .P2(FA1_p), .G1(FA0_g), .P1(FA0_p));
  \Gg和Pg  \gg和pg_1  (
    .P0(FA0_p), .G0(FA0_g), .P1(FA1_p), .G1(FA1_g), .P2(FA2_p), .G2(FA2_g), .P3(FA3_p), .G3(FA3_g), .Gg(Gg),
    .Pg(Pg));

  assign S[3] = F3;
endmodule

module \Gg和Pg  (
  input  P0,
  input  G0,
  input  P1,
  input  G1,
  input  P2,
  input  G2,
  input  P3,
  input  G3,
  output Gg,
  output Pg
);

  wire and_1_out, and_2_out, and_3_out;

  and and_1 (and_1_out, P3, G2);
  and and_2 (and_2_out, P3, P2, G1);
  and and_3 (and_3_out, P3, P2, P1, G0);
  and and_4 (Pg, P3, P2, P1, P0);
  or or_1 (Gg, G3, and_1_out, and_2_out, and_3_out);
endmodule

module \_16位加法器  (
  input  C0,
  input  [15:0] A,
  input  [15:0] B,
  output C4,
  output Cn_1,
  output [15:0] S,
  output Fn_1
);

  wire clu_1_c1, clu_1_c2, clu_1_c3, \n4位加法器_1_gg , \n4位加法器_1_pg , \n4位加法器_2_gg , \n4位加法器_2_pg ,
       \n4位加法器_3_gg , \n4位加法器_3_pg , \n4位加法器_4_gg , \n4位加法器_4_pg ;

  \_4位加法器  \u_4位加法器_1  (
    .B(B[3:0]), .A(A[3:0]), .Gg(\n4位加法器_1_gg ), .Pg(\n4位加法器_1_pg ), .S(S[3:0]), .C0(C0));  // open: C4, C3, F3
  \_4位加法器  \u_4位加法器_2  (
    .B(B[7:4]), .A(A[7:4]), .Gg(\n4位加法器_2_gg ), .Pg(\n4位加法器_2_pg ), .S(S[7:4]), .C0(clu_1_c1));  // open: C4, C3, F3
  \_4位加法器  \u_4位加法器_3  (
    .B(B[11:8]), .A(A[11:8]), .Gg(\n4位加法器_3_gg ), .Pg(\n4位加法器_3_pg ), .S(S[11:8]), .C0(clu_1_c2));  // open: C4, C3, F3
  \_4位加法器  \u_4位加法器_4  (
    .B(B[15:12]), .A(A[15:12]), .Gg(\n4位加法器_4_gg ), .Pg(\n4位加法器_4_pg ), .C4(C4), .S(S[15:12]), .C0(clu_1_c3),
    .C3(Cn_1), .F3(Fn_1));
  CLU clu_1 (
    .C0(C0), .C3(clu_1_c3), .C2(clu_1_c2), .C1(clu_1_c1), .G4(\n4位加法器_4_gg ), .P4(\n4位加法器_4_pg ),
    .G3(\n4位加法器_3_gg ), .P3(\n4位加法器_3_pg ), .G2(\n4位加法器_2_gg ), .P2(\n4位加法器_2_pg ), .G1(\n4位加法器_1_gg ),
    .P1(\n4位加法器_1_pg ));  // open: C4
endmodule

module \_32位加法器  (
  input  C0,
  input  [31:0] A,
  input  [31:0] B,
  output ZF,
  output CF,
  output [31:0] out_6,
  output OF,
  output SF
);

  wire _0_15_c4, _16_31_c4, _16_31_cn_1, or_1_out;

  \_16位加法器  _0_15 (.C0(C0), .A(A[15:0]), .B(B[15:0]), .C4(_0_15_c4), .S(out_6[15:0]));  // open: Cn_1, Fn_1
  \_16位加法器  _16_31 (
    .C0(_0_15_c4), .A(A[31:16]), .B(B[31:16]), .C4(_16_31_c4), .Cn_1(_16_31_cn_1), .S(out_6[31:16]), .Fn_1(SF));
  xor xor_1 (CF, C0, _16_31_c4);
  xor xor_2 (OF, _16_31_c4, _16_31_cn_1);
  not not_1 (ZF, or_1_out);
  or or_1 (or_1_out, out_6[0], out_6[1], out_6[2], out_6[3], out_6[4], out_6[5], out_6[6], out_6[7], out_6[8], out_6[9], out_6[10], out_6[11], out_6[12], out_6[13], out_6[14], out_6[15], out_6[16], out_6[17], out_6[18], out_6[19], out_6[20], out_6[21], out_6[22], out_6[23], out_6[24], out_6[25], out_6[26], out_6[27], out_6[28], out_6[29], out_6[30], out_6[31]);
endmodule

module ALUCtr (
  input  [3:0] Cin,
  output SUBctr,
  output SIGctr,
  output [1:0] OPctr
);

  wire and_1_out, not_2_out, not_3_out;

  or or_1 (SUBctr, Cin[1], Cin[3]);
  not not_1 (SIGctr, Cin[0]);
  not not_2 (not_2_out, Cin[2]);
  not not_3 (not_3_out, Cin[3]);
  and and_1 (and_1_out, not_2_out, Cin[1]);
  and and_2 (OPctr[0], not_3_out, Cin[1]);
  or or_2 (OPctr[1], Cin[0], and_1_out);
endmodule

module ALU (
  input  [3:0] ALUctr,
  input  [31:0] A,
  input  [31:0] B,
  output Zero,
  output [31:0] Result
);

  wire aluctr_1_sigctr, aluctr_1_subctr, multiplexer_2_out, \n32位加法器_1_cf , \n32位加法器_1_of , \n32位加法器_1_sf ,
       xor_2_out, xor_3_out;
  wire [1:0] aluctr_1_opctr;
  wire [31:0] bit_extender_1_out, bit_extender_2_out, \n32位加法器_1_out_6 , or_1_out, xor_1_out;

  assign bit_extender_1_out = {{31{aluctr_1_subctr}}, aluctr_1_subctr};  // Bit_Extender bit_extender_1
  assign or_1_out = A | B;  // OR_Gate or_1, 32 bits wide
  assign xor_1_out = B ^ bit_extender_1_out;  // XOR_Gate xor_1, 32 bits wide
  \_32位加法器  \u_32位加法器_1  (
    .C0(aluctr_1_subctr), .A(A), .B(xor_1_out), .ZF(Zero), .CF(\n32位加法器_1_cf ), .out_6(\n32位加法器_1_out_6 ),
    .OF(\n32位加法器_1_of ), .SF(\n32位加法器_1_sf ));
  xor xor_2 (xor_2_out, aluctr_1_subctr, \n32位加法器_1_cf );
  xor xor_3 (xor_3_out, \n32位加法器_1_of , \n32位加法器_1_sf );
  Multiplexer #(.select(2), .width(32), .enable("false")) multiplexer_1 (
    .in0(\n32位加法器_1_out_6 ), .in1(or_1_out), .in2(B), .in3(bit_extender_2_out), .out(Result),
    .sel(aluctr_1_opctr));
  ALUCtr aluctr_1 (.Cin(ALUctr), .SUBctr(aluctr_1_subctr), .SIGctr(aluctr_1_sigctr), .OPctr(aluctr_1_opctr));
  Multiplexer #(.enable("false")) multiplexer_2 (
    .in0(xor_2_out), .in1(xor_3_out), .out(multiplexer_2_out), .sel(aluctr_1_sigctr));
  assign bit_extender_2_out = {{31{1'b0}}, multiplexer_2_out};  // Bit_Extender bit_extender_2
endmodule

module \指令分解  (
  input  [31:0] \输入指令 ,
  input  [2:0] Extop,
  output [6:0] op,
  output [4:0] rd,
  output [2:0] funct3,
  output [4:0] rs1,
  output [4:0] rs2,
  output [6:0] funct7,
  output [31:0] imm
);

  InstrToimm instrtoimm_1 (.INSTRUCTION(\输入指令 ), .Imm(imm), .EXTOP(Extop));

  assign funct3 = \输入指令 [14:12];
  assign funct7 = \输入指令 [31:25];
  assign op = \输入指令 [6:0];
  assign rd = \输入指令 [11:7];
  assign rs1 = \输入指令 [19:15];
  assign rs2 = \输入指令 [24:20];

  // Notes on the sheet:
  //   立即数扩展
endmodule

module InstrToimm (
  input  [31:0] INSTRUCTION,
  input  [2:0] EXTOP,
  output [31:0] Imm
);

  wire [11:0] bit_extender_4_out;
  wire [19:0] bit_extender_1_out, bit_extender_2_out, bit_extender_3_out;

  assign bit_extender_1_out = {{19{INSTRUCTION[31]}}, INSTRUCTION[31]};  // Bit_Extender bit_extender_1
  assign bit_extender_2_out = {{19{INSTRUCTION[31]}}, INSTRUCTION[31]};  // Bit_Extender bit_extender_2
  assign bit_extender_3_out = {{19{INSTRUCTION[31]}}, INSTRUCTION[31]};  // Bit_Extender bit_extender_3
  assign bit_extender_4_out = {{11{INSTRUCTION[31]}}, INSTRUCTION[31]};  // Bit_Extender bit_extender_4
  Multiplexer #(.select(3), .width(32), .enable("false")) multiplexer_1 (
    .in0({bit_extender_1_out, INSTRUCTION[31:20]}), .in1({INSTRUCTION[31:12], {12{1'b0}}}),
    .in2({bit_extender_2_out, INSTRUCTION[31:25], INSTRUCTION[11:7]}),
    .in3({bit_extender_3_out, INSTRUCTION[7], INSTRUCTION[30:25], INSTRUCTION[11:8], 1'b0}),
    .in4({bit_extender_4_out, INSTRUCTION[19:12], INSTRUCTION[20], INSTRUCTION[30:21], 1'b0}),
    .in5({32{1'b0}}), .in6({32{1'b0}}), .in7({32{1'b0}}), .out(Imm), .sel(EXTOP));

  // Notes on the sheet:
  //   I
  //   U
  //   S
  //   B
  //   J
endmodule

module \取指令部件  (
  input  in_1,
  input  [31:0] imm,
  input  [2:0] extop,
  input  JUMP,
  input  BRANCH,
  input  ZERO,
  output [6:0] op,
  output [4:0] rd,
  output [2:0] funct3,
  output [4:0] rs1,
  output [4:0] rs2,
  output [6:0] funct7,
  output [31:0] imm_2
);

  wire CLK_out, RESET_out;
  wire [31:0] Pc_q, rom_1_data, \下地址逻辑_1_to_pc ;

  Register #(.width(32), .Select("low")) Pc (
    .D(\下地址逻辑_1_to_pc ), .Q(Pc_q), .clk(CLK_out), .clr(RESET_out));  // open: en
  Clock CLK (.out(CLK_out));
  Button RESET (.out(RESET_out));
  \下地址逻辑  \u_下地址逻辑_1  (.PCin(Pc_q), .imm(imm), .JUMP(JUMP), .TO_PC(\下地址逻辑_1_to_pc ), .BRANCH(BRANCH), .ZERO(ZERO));
  ROM #(.addrWidth(12), .dataWidth(32), .Select("low")) rom_1 (.addr(Pc_q[13:2]), .data(rom_1_data), .sel(in_1));
  \指令分解  \u_指令分解_1  (
    .\输入指令 (rom_1_data), .Extop(extop), .op(op), .rd(rd), .funct3(funct3), .rs1(rs1), .rs2(rs2),
    .funct7(funct7), .imm(imm_2));

  // Notes on the sheet:
  //               指令解析器
  //   contents of rom_1 (hex, n*v repeats v):
  //   101 1111 254*0 12b7 fff28293 5de1863 288000ef 112623
endmodule

module \下地址逻辑  (
  input  [31:0] PCin,
  input  [31:0] imm,
  input  JUMP,
  input  BRANCH,
  input  ZERO,
  output [31:0] TO_PC
);

  wire and_1_out, or_1_out;
  wire [31:0] multiplexer_1_out;

  Multiplexer #(.width(32), .enable("false")) multiplexer_1 (
    .in0(32'h4), .in1(imm), .out(multiplexer_1_out), .sel(or_1_out));
  or or_1 (or_1_out, JUMP, and_1_out);
  and and_1 (and_1_out, BRANCH, ZERO);
  \_32位加法器  \u_32位加法器_1  (.C0(1'b0), .A(PCin), .B(multiplexer_1_out), .out_6(TO_PC));  // open: ZF, CF, OF, SF
endmodule

module Registers (
  input  [4:0] RW,
  input  [31:0] busW,
  input  [4:0] RB,
  input  [4:0] RA,
  input  WE,
  input  in_6,
  output [31:0] busA,
  output [31:0] busB
);

  wire and_1_out, and_2_out, and_3_out, and_4_out, and_5_out, and_6_out, and_7_out, and_8_out, and_9_out,
       and_10_out, and_11_out, and_12_out, and_13_out, and_14_out, and_15_out, and_16_out, and_17_out,
       and_18_out, and_19_out, and_20_out, and_21_out, and_22_out, and_23_out, and_24_out, and_25_out,
       and_26_out, and_27_out, and_28_out, and_29_out, and_30_out, and_31_out, and_32_out, decoder_1_out0,
       decoder_1_out1, decoder_1_out2, decoder_1_out3, decoder_1_out4, decoder_1_out5, decoder_1_out6,
       decoder_1_out7, decoder_1_out8, decoder_1_out9, decoder_1_out10, decoder_1_out11, decoder_1_out12,
       decoder_1_out13, decoder_1_out14, decoder_1_out15, decoder_1_out16, decoder_1_out17, decoder_1_out18,
       decoder_1_out19, decoder_1_out20, decoder_1_out21, decoder_1_out22, decoder_1_out23, decoder_1_out24,
       decoder_1_out25, decoder_1_out26, decoder_1_out27, decoder_1_out28, decoder_1_out29, decoder_1_out30,
       decoder_1_out31;
  wire [31:0] \寄存器0_q , \寄存器1_q , \寄存器2_q , \寄存器3_q , \寄存器4_q , \寄存器5_q , \寄存器6_q , \寄存器7_q , \寄存器8_q ,
       \寄存器9_q , \寄存器10_q , \寄存器11_q , \寄存器12_q , \寄存器13_q , \寄存器14_q , \寄存器15_q , \寄存器16_q , \寄存器17_q ,
       \寄存器18_q , \寄存器19_q , \寄存器20_q , \寄存器21_q , \寄存器22_q , \寄存器23_q , \寄存器24_q , \寄存器25_q , \寄存器26_q ,
       \寄存器27_q , \寄存器28_q , \寄存器29_q , \寄存器30_q , \寄存器31_q ;

  Decoder #(.select(5), .enable("false")) decoder_1 (
    .out0(decoder_1_out0), .out1(decoder_1_out1), .out2(decoder_1_out2), .out3(decoder_1_out3),
    .out4(decoder_1_out4), .out5(decoder_1_out5), .out6(decoder_1_out6), .out7(decoder_1_out7),
    .out8(decoder_1_out8), .out9(decoder_1_out9), .out10(decoder_1_out10), .out11(decoder_1_out11),
    .out12(decoder_1_out12), .out13(decoder_1_out13), .out14(decoder_1_out14), .out15(decoder_1_out15),
    .out16(decoder_1_out16), .out17(decoder_1_out17), .out18(decoder_1_out18), .out19(decoder_1_out19),
    .out20(decoder_1_out20), .out21(decoder_1_out21), .out22(decoder_1_out22), .out23(decoder_1_out23),
    .out24(decoder_1_out24), .out25(decoder_1_out25), .out26(decoder_1_out26), .out27(decoder_1_out27),
    .out28(decoder_1_out28), .out29(decoder_1_out29), .out30(decoder_1_out30), .out31(decoder_1_out31),
    .sel(RW));
  and and_1 (and_1_out, WE, in_6, decoder_1_out0);
  and and_2 (and_2_out, WE, in_6, decoder_1_out1);
  and and_3 (and_3_out, WE, in_6, decoder_1_out2);
  and and_4 (and_4_out, WE, in_6, decoder_1_out3);
  and and_5 (and_5_out, WE, in_6, decoder_1_out4);
  and and_6 (and_6_out, WE, in_6, decoder_1_out5);
  and and_7 (and_7_out, WE, in_6, decoder_1_out6);
  and and_8 (and_8_out, WE, in_6, decoder_1_out7);
  and and_9 (and_9_out, decoder_1_out8, in_6, WE);
  and and_10 (and_10_out, decoder_1_out9, in_6, WE);
  and and_11 (and_11_out, decoder_1_out10, in_6, WE);
  and and_12 (and_12_out, decoder_1_out11, in_6, WE);
  and and_13 (and_13_out, decoder_1_out12, in_6, WE);
  and and_14 (and_14_out, decoder_1_out13, in_6, WE);
  and and_15 (and_15_out, decoder_1_out14, in_6, WE);
  and and_16 (and_16_out, in_6, decoder_1_out15, WE);
  and and_17 (and_17_out, decoder_1_out16, in_6, WE);
  and and_18 (and_18_out, decoder_1_out17, in_6, WE);
  and and_19 (and_19_out, decoder_1_out18, in_6, WE);
  and and_20 (and_20_out, decoder_1_out19, in_6, WE);
  and and_21 (and_21_out, decoder_1_out20, in_6, WE);
  and and_22 (and_22_out, decoder_1_out21, in_6, WE);
  and and_23 (and_23_out, decoder_1_out22, in_6, WE);
  and and_24 (and_24_out, decoder_1_out23, in_6, WE);
  and and_25 (and_25_out, decoder_1_out24, in_6, WE);
  and and_26 (and_26_out, decoder_1_out25, in_6, WE);
  and and_27 (and_27_out, decoder_1_out26, in_6, WE);
  and and_28 (and_28_out, decoder_1_out27, in_6, WE);
  and and_29 (and_29_out, decoder_1_out28, in_6, WE);
  and and_30 (and_30_out, decoder_1_out29, in_6, WE);
  and and_31 (and_31_out, decoder_1_out30, in_6, WE);
  and and_32 (and_32_out, decoder_1_out31, in_6, WE);
  Register #(.width(32), .Select("low")) \u_寄存器0  (.D(busW), .en(1'b0), .Q(\寄存器0_q ), .clk(and_1_out));  // open: clr
  Register #(.width(32), .Select("low")) \u_寄存器1  (.D(busW), .Q(\寄存器1_q ), .clk(and_2_out));  // open: en, clr
  Register #(.width(32), .Select("low")) \u_寄存器2  (.D(busW), .Q(\寄存器2_q ), .clk(and_3_out));  // open: en, clr
  Register #(.width(32), .Select("low")) \u_寄存器3  (.D(busW), .Q(\寄存器3_q ), .clk(and_4_out));  // open: en, clr
  Register #(.width(32), .Select("low")) \u_寄存器4  (.D(busW), .Q(\寄存器4_q ), .clk(and_5_out));  // open: en, clr
  Register #(.width(32), .Select("low")) \u_寄存器5  (.D(busW), .Q(\寄存器5_q ), .clk(and_6_out));  // open: en, clr
  Register #(.width(32), .Select("low")) \u_寄存器6  (.D(busW), .Q(\寄存器6_q ), .clk(and_7_out));  // open: en, clr
  Register #(.width(32), .Select("low")) \u_寄存器7  (.D(busW), .Q(\寄存器7_q ), .clk(and_8_out));  // open: en, clr
  Register #(.width(32), .Select("low")) \u_寄存器8  (.D(busW), .Q(\寄存器8_q ), .clk(and_9_out));  // open: en, clr
  Register #(.width(32), .Select("low")) \u_寄存器9  (.D(busW), .Q(\寄存器9_q ), .clk(and_10_out));  // open: en, clr
  Register #(.width(32), .Select("low")) \u_寄存器10  (.D(busW), .Q(\寄存器10_q ), .clk(and_11_out));  // open: en, clr
  Register #(.width(32), .Select("low")) \u_寄存器11  (.D(busW), .Q(\寄存器11_q ), .clk(and_12_out));  // open: en, clr
  Register #(.width(32), .Select("low")) \u_寄存器12  (.D(busW), .Q(\寄存器12_q ), .clk(and_13_out));  // open: en, clr
  Register #(.width(32), .Select("low")) \u_寄存器13  (.D(busW), .Q(\寄存器13_q ), .clk(and_14_out));  // open: en, clr
  Register #(.width(32), .Select("low")) \u_寄存器14  (.D(busW), .Q(\寄存器14_q ), .clk(and_15_out));  // open: en, clr
  Register #(.width(32), .Select("low")) \u_寄存器15  (.D(busW), .Q(\寄存器15_q ), .clk(and_16_out));  // open: en, clr
  Register #(.width(32), .Select("low")) \u_寄存器16  (.D(busW), .Q(\寄存器16_q ), .clk(and_17_out));  // open: en, clr
  Register #(.width(32), .Select("low")) \u_寄存器17  (.D(busW), .Q(\寄存器17_q ), .clk(and_18_out));  // open: en, clr
  Register #(.width(32), .Select("low")) \u_寄存器18  (.D(busW), .Q(\寄存器18_q ), .clk(and_19_out));  // open: en, clr
  Register #(.width(32), .Select("low")) \u_寄存器19  (.D(busW), .Q(\寄存器19_q ), .clk(and_20_out));  // open: en, clr
  Register #(.width(32), .Select("low")) \u_寄存器20  (.D(busW), .Q(\寄存器20_q ), .clk(and_21_out));  // open: en, clr
  Register #(.width(32), .Select("low")) \u_寄存器21  (.D(busW), .Q(\寄存器21_q ), .clk(and_22_out));  // open: en, clr
  Register #(.width(32), .Select("low")) \u_寄存器22  (.D(busW), .Q(\寄存器22_q ), .clk(and_23_out));  // open: en, clr
  Register #(.width(32), .Select("low")) \u_寄存器23  (.D(busW), .Q(\寄存器23_q ), .clk(and_24_out));  // open: en, clr
  Register #(.width(32), .Select("low")) \u_寄存器24  (.D(busW), .Q(\寄存器24_q ), .clk(and_25_out));  // open: en, clr
  Register #(.width(32), .Select("low")) \u_寄存器25  (.D(busW), .Q(\寄存器25_q ), .clk(and_26_out));  // open: en, clr
  Register #(.width(32), .Select("low")) \u_寄存器26  (.D(busW), .Q(\寄存器26_q ), .clk(and_27_out));  // open: en, clr
  Register #(.width(32), .Select("low")) \u_寄存器27  (.D(busW), .Q(\寄存器27_q ), .clk(and_28_out));  // open: en, clr
  Register #(.width(32), .Select("low")) \u_寄存器28  (.D(busW), .Q(\寄存器28_q ), .clk(and_29_out));  // open: en, clr
  Register #(.width(32), .Select("low")) \u_寄存器29  (.D(busW), .Q(\寄存器29_q ), .clk(and_30_out));  // open: en, clr
  Register #(.width(32), .Select("low")) \u_寄存器30  (.D(busW), .Q(\寄存器30_q ), .clk(and_31_out));  // open: en, clr
  Register #(.width(32), .Select("low")) \u_寄存器31  (.D(busW), .Q(\寄存器31_q ), .clk(and_32_out));  // open: en, clr
  Multiplexer #(.select(5), .width(32), .enable("false")) multiplexer_1 (
    .in0(\寄存器0_q ), .in1(\寄存器1_q ), .in2(\寄存器2_q ), .in3(\寄存器3_q ), .in4(\寄存器4_q ), .in5(\寄存器5_q ),
    .in6(\寄存器6_q ), .in7(\寄存器7_q ), .in8(\寄存器8_q ), .in9(\寄存器9_q ), .in10(\寄存器10_q ), .in11(\寄存器11_q ),
    .in12(\寄存器12_q ), .in13(\寄存器13_q ), .in14(\寄存器14_q ), .in15(\寄存器15_q ), .in16(\寄存器16_q ),
    .in17(\寄存器17_q ), .in18(\寄存器18_q ), .in19(\寄存器19_q ), .in20(\寄存器20_q ), .in21(\寄存器21_q ),
    .in22(\寄存器22_q ), .in23(\寄存器23_q ), .in24(\寄存器24_q ), .in25(\寄存器25_q ), .in26(\寄存器26_q ),
    .in27(\寄存器27_q ), .in28(\寄存器28_q ), .in29(\寄存器29_q ), .in30(\寄存器30_q ), .in31(\寄存器31_q ), .out(busA),
    .sel(RA));
  Multiplexer #(.select(5), .width(32), .enable("false")) multiplexer_2 (
    .in0(\寄存器0_q ), .in1(\寄存器1_q ), .in2(\寄存器2_q ), .in3(\寄存器3_q ), .in4(\寄存器4_q ), .in5(\寄存器5_q ),
    .in6(\寄存器6_q ), .in7(\寄存器7_q ), .in8(\寄存器8_q ), .in9(\寄存器9_q ), .in10(\寄存器10_q ), .in11(\寄存器11_q ),
    .in12(\寄存器12_q ), .in13(\寄存器13_q ), .in14(\寄存器14_q ), .in15(\寄存器15_q ), .in16(\寄存器16_q ),
    .in17(\寄存器17_q ), .in18(\寄存器18_q ), .in19(\寄存器19_q ), .in20(\寄存器20_q ), .in21(\寄存器21_q ),
    .in22(\寄存器22_q ), .in23(\寄存器23_q ), .in24(\寄存器24_q ), .in25(\寄存器25_q ), .in26(\寄存器26_q ),
    .in27(\寄存器27_q ), .in28(\寄存器28_q ), .in29(\寄存器29_q ), .in30(\寄存器30_q ), .in31(\寄存器31_q ), .out(busB),
    .sel(RB));
endmodule

module CPU (
);

  wire alu_1_zero, and_1_out, button_1_out, button_2_out, clock_1_out, clock_2_out, clock_3_out, not_1_out,
       or_1_out, \控制部件_1_aluasrc , \控制部件_1_branch , \控制部件_1_jump , \控制部件_1_memtoreg , \控制部件_1_memwr ,
       \控制部件_1_regwr ;
  wire [1:0] \控制部件_1_alubsrc ;
  wire [2:0] \指令分解_1_funct3 , \控制部件_1_extop ;
  wire [3:0] \控制部件_1_aluctr_3_0 ;
  wire [4:0] \指令分解_1_rd , \指令分解_1_rs1 , \指令分解_1_rs2 ;
  wire [6:0] \指令分解_1_op ;
  wire [11:0] pc_q_2;
  wire [31:0] adder_1_out, alu_1_result, multiplexer_1_out, multiplexer_2_out, multiplexer_3_out,
       multiplexer_4_out, pc_q, registers_1_busa, registers_1_busb, \指令分解_1_imm , \指令存储器_data , \数据存储器_data ;

  Clock clock_1 (.out(clock_1_out));
  Clock clock_2 (.out(clock_2_out));
  \指令分解  \u_指令分解_1  (
    .\输入指令 (\指令存储器_data ), .Extop(\控制部件_1_extop ), .op(\指令分解_1_op ), .rd(\指令分解_1_rd ),
    .funct3(\指令分解_1_funct3 ), .rs1(\指令分解_1_rs1 ), .rs2(\指令分解_1_rs2 ), .imm(\指令分解_1_imm ));  // open: funct7
  ROM #(.addrWidth(12), .dataWidth(32), .Select("low")) \u_指令存储器  (.addr(pc_q_2), .data(\指令存储器_data ));
  Registers registers_1 (
    .RW(\指令分解_1_rd ), .busW(multiplexer_4_out), .RB(\指令分解_1_rs2 ), .RA(\指令分解_1_rs1 ), .WE(\控制部件_1_regwr ),
    .in_6(clock_2_out), .busA(registers_1_busa), .busB(registers_1_busb));
  Register #(.width(32), .trigger("falling"), .Select("low")) pc (
    .D(adder_1_out), .Q({pc_q[31:14], pc_q_2, pc_q[1:0]}), .clk(clock_1_out), .clr(button_1_out));  // open: en
  Button button_1 (.out(button_1_out));
  Multiplexer #(.width(32), .enable("false")) multiplexer_1 (
    .in0(registers_1_busa), .in1({pc_q[31:14], pc_q_2, pc_q[1:0]}), .out(multiplexer_1_out),
    .sel(\控制部件_1_aluasrc ));
  Multiplexer #(.select(2), .width(32), .enable("false")) multiplexer_2 (
    .in0(registers_1_busb), .in1(32'h4), .in2(\指令分解_1_imm ), .out(multiplexer_2_out), .sel(\控制部件_1_alubsrc ));  // open: in3
  Adder #(.width(32)) adder_1 (
    .a({pc_q[31:14], pc_q_2, pc_q[1:0]}), .b(multiplexer_3_out), .out(adder_1_out));  // open: cin, cout
  Multiplexer #(.width(32), .enable("false")) multiplexer_3 (
    .in0(32'h4), .in1(\指令分解_1_imm ), .out(multiplexer_3_out), .sel(or_1_out));
  ALU alu_1 (
    .Zero(alu_1_zero), .Result(alu_1_result), .A(multiplexer_1_out), .B(multiplexer_2_out),
    .ALUctr(\控制部件_1_aluctr_3_0 ));
  or or_1 (or_1_out, and_1_out, \控制部件_1_jump );
  and and_1 (and_1_out, alu_1_zero, \控制部件_1_branch );
  Clock clock_3 (.out(clock_3_out));
  RAM #(.addrWidth(12), .dataWidth(32), .bus("separate"), .Select("high")) \u_数据存储器  (
    .addr(alu_1_result[13:2]), .din(registers_1_busb), .data(\数据存储器_data ), .str(\控制部件_1_memwr ),
    .clk(clock_3_out), .ld(not_1_out), .clr(button_2_out));  // open: sel
  not not_1 (not_1_out, \控制部件_1_memwr );
  Button button_2 (.out(button_2_out));
  \控制部件  \u_控制部件_1  (
    .funct3(\指令分解_1_funct3 ), .REGwr(\控制部件_1_regwr ), .MEMTOREG(\控制部件_1_memtoreg ), .MEMWR(\控制部件_1_memwr ),
    .BRANCH(\控制部件_1_branch ), .JUMP(\控制部件_1_jump ), .ALUctr_3_0(\控制部件_1_aluctr_3_0 ),
    .ALUASrc(\控制部件_1_aluasrc ), .ALUBSrc(\控制部件_1_alubsrc ), .EXTOP(\控制部件_1_extop ), .OP_6_0(\指令分解_1_op ));
  Multiplexer #(.width(32), .enable("false")) multiplexer_4 (
    .in0(alu_1_result), .in1(\数据存储器_data ), .out(multiplexer_4_out), .sel(\控制部件_1_memtoreg ));

  // Notes on the sheet:
  //   contents of 指令存储器 (hex, n*v repeats v):
  //   2183 106093 106113 120233 308663 2080b3 ff5ff06f 402223 ffdff06f
endmodule

module \控制部件  (
  input  [6:0] OP_6_0,
  input  [2:0] funct3,
  output REGwr,
  output MEMTOREG,
  output MEMWR,
  output BRANCH,
  output JUMP,
  output [3:0] ALUctr_3_0,
  output ALUASrc,
  output [1:0] ALUBSrc,
  output [2:0] EXTOP
);

  wire and_1_out, and_2_out, and_3_out, and_4_out, and_5_out, and_6_out, and_7_out, \I型_out , Lui_out,
       not_1_out, not_2_out, not_3_out, or_1_out, or_2_out, \R型_out ;

  and \R型  (\R型_out , ~OP_6_0[6], OP_6_0[5], OP_6_0[4], ~OP_6_0[3], ~OP_6_0[2], OP_6_0[1], OP_6_0[0]);  // AND_Gate
  and \I型  (\I型_out , ~OP_6_0[6], ~OP_6_0[5], OP_6_0[4], ~OP_6_0[3], ~OP_6_0[2], OP_6_0[1], OP_6_0[0]);  // AND_Gate
  or or_1 (or_1_out, \R型_out , \I型_out );
  and and_1 (and_1_out, or_1_out, funct3[2]);
  and and_2 (and_2_out, or_1_out, funct3[1]);
  and and_3 (and_3_out, or_1_out, funct3[0]);
  and Lui (Lui_out, ~OP_6_0[6], OP_6_0[5], OP_6_0[4], ~OP_6_0[3], OP_6_0[2], OP_6_0[1], OP_6_0[0]);  // AND_Gate
  and Load (MEMTOREG, ~OP_6_0[6], ~OP_6_0[5], ~OP_6_0[4], ~OP_6_0[3], ~OP_6_0[2], OP_6_0[1], OP_6_0[0]);  // AND_Gate
  and and_4 (and_4_out, \I型_out , funct3[1], funct3[2]);
  and Store (MEMWR, ~OP_6_0[6], OP_6_0[5], ~OP_6_0[4], ~OP_6_0[3], ~OP_6_0[2], OP_6_0[1], OP_6_0[0]);  // AND_Gate
  or or_2 (or_2_out, MEMTOREG, MEMWR);
  and \B型  (BRANCH, OP_6_0[6], OP_6_0[5], ~OP_6_0[4], ~OP_6_0[3], ~OP_6_0[2], OP_6_0[1], OP_6_0[0]);  // AND_Gate
  not not_1 (not_1_out, funct3[0]);
  not not_2 (not_2_out, funct3[1]);
  not not_3 (not_3_out, funct3[2]);
  and \J型  (ALUASrc, OP_6_0[6], OP_6_0[5], ~OP_6_0[4], OP_6_0[3], OP_6_0[2], OP_6_0[1], OP_6_0[0]);  // AND_Gate
  and and_5 (and_5_out, or_2_out, funct3[1]);
  and and_6 (and_6_out, MEMWR, funct3[1]);
  and and_7 (and_7_out, BRANCH, not_1_out, not_2_out, not_3_out);
  or or_3 (REGwr, \R型_out , \I型_out , Lui_out, MEMTOREG, ALUASrc);
  or or_4 (ALUctr_3_0[3], Lui_out, BRANCH);
  or or_5 (ALUctr_3_0[2], Lui_out, and_1_out);
  or or_6 (ALUctr_3_0[1], Lui_out, and_2_out);
  or or_7 (ALUctr_3_0[0], Lui_out, and_3_out);
  or or_8 (ALUBSrc[1], and_5_out, Lui_out, and_4_out);
  or or_9 (EXTOP[1], and_6_out, and_7_out);
  or or_10 (EXTOP[0], Lui_out, and_7_out);

  assign ALUBSrc[0] = ALUASrc;
  assign EXTOP[2] = ALUASrc;
  assign JUMP = ALUASrc;
endmodule
